// Digital circuit main.dig as structural Verilog
module main (
  input  Clock,
  input  [31:0] in_3,
  output [15:0] Imediato
);

  wire [4:0] multiplexer_1_out;
  wire [5:0] OPCODE;
  wire [25:16] instruction_mem_1__32b__out;
  wire [31:0] _32x32_1_r_d1, _32x32_1_r_d2, add_1_s, bitextender_1_out, multiplexer_2_out, pc_1_pc_out, R31,
       ramasync_1_q, ula_1_resultado;

  PC pc_1 (.Clok(Clock), .PC_IN(add_1_s), .PC_OUT(pc_1_pc_out));
  Add #(.Bits(32)) add_1 (.a(pc_1_pc_out), .b(32'h4), .c_i(1'b0), .s(add_1_s));  // open: c_o
  instruction_mem instruction_mem_1 (
    ._32b__ADDR(pc_1_pc_out), ._1b__Enable(Clock), ._32b__Out({OPCODE, instruction_mem_1__32b__out, Imediato}));
  Multiplexer #(.Bits(5)) multiplexer_1 (
    .sel(1'b0), .in_0(instruction_mem_1__32b__out[20:16]), .in_1(Imediato[15:11]), .out(multiplexer_1_out));
  _32x32 _32x32_1 (
    ._32_W_d(in_3), ._5__R_reg1(instruction_mem_1__32b__out[25:21]),
    ._5__R_reg2(instruction_mem_1__32b__out[20:16]), ._5b__A_set(multiplexer_1_out), .Clk(Clock),
    ._1__W_e(1'b1), .R_d1(_32x32_1_r_d1), .R_d2(_32x32_1_r_d2), .R31(R31));
  BitExtender #(.inputBits(16), .outputBits(32)) bitextender_1 (.in(Imediato), .out(bitextender_1_out));
  Seven_Seg_Hex seven_seg_hex_1 (.d(R31[19:16]), .dp(1'b0));
  Seven_Seg_Hex seven_seg_hex_2 (.d(R31[15:12]), .dp(1'b0));
  Seven_Seg_Hex seven_seg_hex_3 (.d(R31[11:8]), .dp(1'b0));
  Multiplexer #(.Bits(32)) multiplexer_2 (
    .sel(1'b0), .in_0(_32x32_1_r_d2), .in_1(bitextender_1_out), .out(multiplexer_2_out));
  ula ula_1 (
    .ALUControl(4'b0000), .A(_32x32_1_r_d1), .B(multiplexer_2_out), .Shamt({6{1'b0}}),
    .Resultado(ula_1_resultado));  // open: Zero
  Seven_Seg_Hex seven_seg_hex_4 (.d(R31[7:4]), .dp(1'b0));
  Seven_Seg_Hex seven_seg_hex_5 (.d(R31[3:0]), .dp(1'b0));
  RAMAsync #(.AddrBits(24), .Bits(32)) ramasync_1 (
    .A(ula_1_resultado[23:0]), .D(_32x32_1_r_d2), .we(1'b0), .Q(ramasync_1_q));
  Multiplexer #(.Bits(32)) multiplexer_3 (.sel(1'b0), .in_0(ramasync_1_q), .in_1(ula_1_resultado));  // open: out

  // Other names for the same wires on the sheet: WB[31:0] = in_3

  // Notes on the sheet:
  //   in_3: default 707258
endmodule
